# Fritzing sketch RiCino_pro_1_1 (saved by Fritzing 0.7.7b)
breadboards: 1

parts:
  U1 = Arduino Mega
  LCD1 = LCD screen
  LED1 = LED - 5mm [color="Red (633nm)" package="5 mm [THT]"]
  U2 = Voltage Regulator - 5V [package="TO220 [THT]"]
  VCC1 = Battery block 9V
  R1 = Trimmer Potentiometer [maximum_resistance=10kΩ package=THT]
  R2 = Trimmer Potentiometer [maximum_resistance=10kΩ package=THT]
  R3 = Resistor [tolerance=±5% resistance=10k package=THT]
  R4 = Resistor [tolerance=±5% resistance=10k package=THT]
  R5 = Resistor [tolerance=±5% resistance=10k package=THT]
  R6 = Resistor [tolerance=±5% resistance=10k package=THT]
  S1 = Pushbutton [package="[THT]"]
  S2 = Pushbutton [package="[THT]"]
  S3 = Pushbutton [package="[THT]"]
  S4 = Pushbutton [package="[THT]"]
  R7 = Resistor [tolerance=±5% resistance=470 package=THT]
  U3 = mystery part, 3 pins [chip_label=?]
  U4 = mystery part, 3 pins [chip_label=?]
  J1 = Piezo Speaker
  U5 = mystery part, 7 pins [chip_label=?]
  R8 = Resistor [tolerance=±5% resistance=150 package=THT]
  Parte1 = Real Time Clock Module - DS1307 RTC Breakout Board
  Parte2 = Bluetooth Module Breakout - Roving Networks (RN-41)

nets:
  GND: U1.GND, LCD1.VSS, LCD1.R/W, LCD1.LED-, LED1.cathode, U2.GND, VCC1.-, R1.leg1, R2.leg1, S1.Pin_3, S1.Pin_4, S2.Pin_3, S2.Pin_4, S3.Pin_3, S3.Pin_4, S4.Pin_3, S4.Pin_4, U3.pin1, U4.pin1, J1.pin1, U5.pin7, Parte1.GND, Parte2.GND, Parte2.RESET
  N1: U1.D12, U3.pin3
  N2: U1.D9, R6.Pin_0, S4.Pin_1, S4.Pin_2
  N3: U1.D8, R5.Pin_0, S3.Pin_1, S3.Pin_2
  N4: U1.D7, R4.Pin_0, S2.Pin_1, S2.Pin_2
  N5: U1.D6, R3.Pin_0, S1.Pin_1, S1.Pin_2
  N6: U1.D2, R8.Pin_1
  N7: U1.D1TX, Parte2.UARTRX
  N8: U1.D0RX, Parte2.UARTRTS, Parte2.UARTTX
  3V3: U1.3V3, U5.pin5, Parte2.VCC
  VIN: U1.VIN, LCD1.VDD, U2.output_voltage, R1.leg2, R2.leg2, R3.Pin_1, R4.Pin_1, R5.Pin_1, R6.Pin_1, R7.Pin_0, U3.pin2, U4.pin2, U5.pin6, Parte1.5V
  N9: U1.D20, Parte1.SDA
  N10: U1.D21, Parte1.SCL
  N11: U1.D22, LCD1.DB7
  N12: U1.D24, LCD1.DB6
  N13: U1.D26, LCD1.DB5
  N14: U1.D28, LCD1.DB4
  N15: U1.D30, LCD1.E
  N16: U1.D32, LCD1.RS
  N17: U1.D34, J1.pin2
  N18: U1.D50, U5.pin1
  N19: U1.D51, U5.pin2
  N20: U1.D52, U5.pin4
  N21: U1.D53, U5.pin3
  N22: LCD1.V0, R1.wiper
  N23: LCD1.LED+, R2.wiper
  N24: LED1.anode, R7.Pin_1
  N25: U2.input_voltage, VCC1.+
  N26: U4.pin3, R8.Pin_0

notes:
  RF EMITER
  Receptor IR TSOP
  BUZZER
  SD CARD READER
  MISO
  MOSI
  CS
  CLK
  3,3v
  5v
  -
  < > ^ v
  7805
  BLUETOOTH
  RTC DS1307
